# Fritzing sketch schematics (saved by Fritzing 0.9.3b)
breadboards: 1

parts:
  MCU1 = Raspberry Pi Zero
  Q1 = MOSFET-NCHANNEL [package=to220v]
  Q2 = MOSFET-NCHANNEL [package=to220v]
  Q3 = MOSFET-NCHANNEL [package=to220v]
  LED1 = smd LED [color="Red (633nm)" package="0603 [SMD]"]
  R1 = Resistor [tolerance=±20% resistance=330 package="1206 [SMD]"]
  M1 = DC Motor
  VCC1 = Battery
  VCC2 = Battery  # not connected
  M2 = DC Motor
  M3 = DC Motor
  VCC3 = Battery  # not connected
  RHT1 = Humidity and Temperature Sensor RHT03  # not connected
  DS1 = DS18B20 1-Wire Temperature Sensor [part_number=DS18B20]  # not connected

nets:
  N1: MCU1.pin_6, MCU1.pin_8, MCU1.pin_14, MCU1.pin_34, MCU1.pin_39, Q1.G, Q1.S, Q2.S, Q3.S, R1.Pin_0, VCC1.-
  N2: MCU1.pin_10, Q3.G
  N3: MCU1.pin_12, Q2.G
  N4: MCU1.pin_40, LED1.anode
  N5: Q1.D, M1.pin_1
  N6: Q3.D, M2.pin_1, M3.pin_1
  N7: LED1.cathode, R1.Pin_1

notes:
  Water pump
  12V from ATX PSU
  PC fans (not motors]
  5V from ATX PSU
  DHT22
